# Fritzing sketch gaming_sandogasa (saved by Fritzing 0.9.5d)
breadboards: 1

parts:
  パーツ1 = Arduino Uno (Rev3)
  U3 = WS2812 RGB LED matrix 1x8
  パーツ2 = SRF05 Ultrasonic Rangefinder

nets:
  N1: パーツ1.D12/MISO, パーツ2.Echo
  N2: パーツ1.D13/SCK, パーツ2.Trig
  N3: パーツ1.D3_PWM, U3.DIN
  VCC: パーツ1.5V, U3.VCC, パーツ2.VCC
  GND: U3.GND, パーツ2.GND

custom parts:
  WS2812 RGB LED matrix 1x8: WS2812 matrix 1x8
